# Fritzing sketch 3X3X3_RGB (saved by Fritzing 0.9.3b)
circuit board: 8.5cm x 5cm
perfboards: 1

parts:
  Nano1 = Arduino Nano (Rev3.0)
  U1 = 74HC595 [package="DIP16 [THT]"]
  U2 = 74HC595 [package="DIP16 [THT]"]
  B11 = female pin header, 1 pin [form="♀ (female)"]
  G11 = female pin header, 1 pin [form="♀ (female)"]
  R11 = female pin header, 1 pin [form="♀ (female)"]
  B21 = female pin header, 1 pin [form="♀ (female)"]
  G21 = female pin header, 1 pin [form="♀ (female)"]
  R21 = female pin header, 1 pin [form="♀ (female)"]
  B31 = female pin header, 1 pin [form="♀ (female)"]
  G31 = female pin header, 1 pin [form="♀ (female)"]
  R31 = female pin header, 1 pin [form="♀ (female)"]
  B12 = female pin header, 1 pin [form="♀ (female)"]
  G12 = female pin header, 1 pin [form="♀ (female)"]
  R12 = female pin header, 1 pin [form="♀ (female)"]
  B22 = female pin header, 1 pin [form="♀ (female)"]
  G22 = female pin header, 1 pin [form="♀ (female)"]
  R22 = female pin header, 1 pin [form="♀ (female)"]
  B32 = female pin header, 1 pin [form="♀ (female)"]
  G32 = female pin header, 1 pin [form="♀ (female)"]
  R32 = female pin header, 1 pin [form="♀ (female)"]
  B13 = female pin header, 1 pin [form="♀ (female)"]
  G13 = female pin header, 1 pin [form="♀ (female)"]
  R13 = female pin header, 1 pin [form="♀ (female)"]
  B23 = female pin header, 1 pin [form="♀ (female)"]
  G23 = female pin header, 1 pin [form="♀ (female)"]
  R23 = female pin header, 1 pin [form="♀ (female)"]
  B33 = female pin header, 1 pin [form="♀ (female)"]
  G33 = female pin header, 1 pin [form="♀ (female)"]
  R33 = female pin header, 1 pin [form="♀ (female)"]
  G1 = female pin header, 1 pin [form="♀ (female)"]
  G2 = female pin header, 1 pin [form="♀ (female)"]
  G3 = female pin header, 1 pin [form="♀ (female)"]
  G4 = female pin header, 1 pin [form="♀ (female)"]
  G5 = female pin header, 1 pin [form="♀ (female)"]
  G6 = female pin header, 1 pin [form="♀ (female)"]
  G7 = female pin header, 1 pin [form="♀ (female)"]
  G8 = female pin header, 1 pin [form="♀ (female)"]
  G9 = female pin header, 1 pin [form="♀ (female)"]
  -_+ = female pin header, 2 pins [form="♀ (female)"]

nets:
  GND: Nano1.GND, U1.GND, U1.OE, U2.GND, U2.OE, -_+.pin2
  N1: Nano1.D2, G8.pin1
  N2: Nano1.D3, G9.pin1
  N3: Nano1.D10, U1.ST_CP, U2.ST_CP
  N4: Nano1.D11/MOSI, U1.DS
  VCC: Nano1.5V, U1.MR, U1.VCC, U2.MR, U2.VCC, -_+.pin1
  N5: Nano1.D13/SCK, U1.SH_CP, U2.SH_CP
  N6: U1.Q1, R21.pin1, R22.pin1, R23.pin1
  N7: U1.Q2, R31.pin1, R32.pin1, R33.pin1
  N8: U1.Q3, G11.pin1, G12.pin1, G13.pin1
  N9: U1.Q4, G21.pin1, G22.pin1, G23.pin1
  N10: U1.Q5, G31.pin1, G32.pin1, G33.pin1
  N11: U1.Q6, B11.pin1, B12.pin1, B13.pin1
  N12: U1.Q7, B21.pin1, B22.pin1, B23.pin1
  N13: U1.Q7', U2.DS
  N14: U1.Q0, R11.pin1, R12.pin1, R13.pin1
  N15: U2.Q1, G1.pin1
  N16: U2.Q2, G2.pin1
  N17: U2.Q3, G3.pin1
  N18: U2.Q4, G4.pin1
  N19: U2.Q5, G5.pin1
  N20: U2.Q6, G6.pin1
  N21: U2.Q7, G7.pin1
  N22: U2.Q0, B31.pin1, B32.pin1, B33.pin1

notes:
  Ground Connections for LEDs (add 150Ω resistor when soldering)
  LED Connections (colours match)
  Hole for wireless ↑ charging reciever module below
